# Fritzing sketch schematic (saved by Fritzing 0.9.2b)
breadboards: 1

parts:
  LCD1 = LCD screen
  R1 = Photocell (LDR) [package=THT]
  T1 = LM35 Temperature Sensor [package="TO92 [THT]"]
  U1 = Barometric Pressure Sensor
  RHT1 = Humidity and Temperature Sensor RHT03
  Raspberry_Pi_B_rev1 = Raspberry Pi B rev1
  IC1 = MCP3008 8-channel 10-bit ADC [part_number=MCP3008]
  R2 = Resistor [tolerance=±5% resistance=1k package=THT]
  R3 = Resistor [tolerance=±5% resistance=10k package=THT]
  R4 = Trimmer Potentiometer [maximum_resistance=10kΩ package=THT]
  R5 = Resistor [tolerance=±5% resistance=10k package=THT]
  R6 = Resistor [tolerance=±5% resistance=20k package=THT]
  IC2 = IC, DIP package, 4 pins [chip_label="Air Sensor"]

nets:
  GND: LCD1.VSS, LCD1.R/W, LCD1.LED-, T1.GND, U1.GND, RHT1.GND_2, Raspberry_Pi_B_rev1.GND, IC1.no_name_yet#9, IC1.no_name_yet#14, R2.Pin_1, R4.leg1, R6.Pin_0, IC2.pin1
  VDD: LCD1.VDD, LCD1.LED+, Raspberry_Pi_B_rev1.5V, R4.leg2, IC2.pin3, IC2.pin4
  N1: LCD1.V0, R4.wiper
  N2: LCD1.RS, Raspberry_Pi_B_rev1.GIPO_0
  N3: LCD1.E, Raspberry_Pi_B_rev1.GIPO_1
  N4: LCD1.DB4, Raspberry_Pi_B_rev1.GPIO_24
  N5: LCD1.DB5, Raspberry_Pi_B_rev1.GPIO_25
  N6: LCD1.DB6, Raspberry_Pi_B_rev1.GPIO_23
  N7: LCD1.DB7, Raspberry_Pi_B_rev1.GPIO_21
  3.3V: R1.pin_0, T1.+Vs, U1.3.3V, RHT1.Vcc, Raspberry_Pi_B_rev1.3V3, IC1.no_name_yet#15, IC1.no_name_yet#16, R3.Pin_0
  N8: R1.pin_1, IC1.no_name_yet#1, R2.Pin_0
  N9: T1.Vout, IC1.no_name_yet#3
  N10: U1.CSB, Raspberry_Pi_B_rev1.GPIO_7
  N11: U1.MISO, Raspberry_Pi_B_rev1.GPIO_9, IC1.no_name_yet#12
  N12: U1.MOSI, Raspberry_Pi_B_rev1.GPIO_10, IC1.no_name_yet#11
  N13: U1.SCK, Raspberry_Pi_B_rev1.GPIO_11, IC1.no_name_yet#13
  N14: RHT1.Data-signal, Raspberry_Pi_B_rev1.GPIO_14, R3.Pin_1
  N15: Raspberry_Pi_B_rev1.GPIO_8, IC1.no_name_yet#10
  N16: IC1.no_name_yet#2, R5.Pin_0, R6.Pin_1
  N17: R5.Pin_1, IC2.pin2
